// Logisim project GROUP_25.circ as structural Verilog: 10 circuits, main circuit CPU
module ARITHMETIC_LOGIC_UNIT (
  input  [15:0] A,
  input  [15:0] B,
  input  [3:0] AUSel,
  input  [2:0] RUSel,
  input  OE,
  output [15:0] AUDout,
  output [15:0] AUResult,
  output RUResult
);

  wire [15:0] arithmetic_unit_1_audout;

  assign AUDout = OE ? arithmetic_unit_1_audout : 16'bz;  // Controlled_Buffer controlled_buffer_1
  ARITHMETIC_UNIT arithmetic_unit_1 (
    .A(A), .B(B), .AUSel(AUSel), .AUDout(arithmetic_unit_1_audout), .AUResult(AUResult));
  RELATIONAL_UNIT relational_unit_1 (.A(A), .B(B), .RUSel(RUSel), .RUResult(RUResult));
endmodule

module ARITHMETIC_UNIT (
  input  [15:0] A,
  input  [15:0] B,
  input  [3:0] AUSel,
  output [15:0] AUDout,
  output [15:0] AUResult
);

  wire [15:0] adder_1_out, and_1_out, divider_1_out, divider_1_rem, multiplier_1_out, negator_1_out,
       negator_2_out, or_1_out, shifter_1_out, shifter_2_out, shifter_3_out, shifter_4_out, subtractor_1_out,
       xor_1_out;

  Adder #(.width(16)) adder_1 (.a(A), .b(B), .out(adder_1_out));  // open: cin, cout
  assign and_1_out = A & B;  // AND_Gate and_1, 16 bits wide
  assign or_1_out = A | B;  // OR_Gate or_1, 16 bits wide
  assign xor_1_out = A ^ B;  // XOR_Gate xor_1, 16 bits wide
  Divider #(.width(16)) divider_1 (.a(A), .b(B), .out(divider_1_out), .rem(divider_1_rem));  // open: upper
  Multiplier #(.width(16)) multiplier_1 (.a(A), .b(B), .out(multiplier_1_out));  // open: cin, cout
  Subtractor #(.width(16)) subtractor_1 (.a(A), .b(B), .out(subtractor_1_out));  // open: bin, bout
  Shifter #(.width(16)) shifter_1 (.in(A), .\dist (4'b0010), .out(shifter_1_out));
  Shifter #(.width(16)) shifter_2 (.in(B), .\dist (4'b0010), .out(shifter_2_out));
  Shifter #(.shift("lr"), .width(16)) shifter_3 (.in(A), .\dist (4'b0010), .out(shifter_3_out));
  Shifter #(.shift("lr"), .width(16)) shifter_4 (.in(B), .\dist (4'b0010), .out(shifter_4_out));
  Negator #(.width(16)) negator_1 (.in(A), .out(negator_1_out));
  Negator #(.width(16)) negator_2 (.in(B), .out(negator_2_out));
  Multiplexer #(.select(4), .width(16)) multiplexer_1 (
    .in0(adder_1_out), .in1(and_1_out), .in2(or_1_out), .in3(xor_1_out), .in4(divider_1_out),
    .in5(divider_1_rem), .in6(multiplier_1_out), .in7(subtractor_1_out), .in8(shifter_1_out),
    .in9(shifter_2_out), .in10(shifter_3_out), .in11(shifter_4_out), .in12(negator_1_out),
    .in13(negator_2_out), .out(AUDout), .sel(AUSel));  // open: in14, in15

  assign AUResult = AUDout;
endmodule

module RELATIONAL_UNIT (
  input  [15:0] A,
  input  [15:0] B,
  input  [2:0] RUSel,
  output RUResult
);

  wire comparator_1_eq, comparator_1_gt, comparator_1_lt, not_1_out, or_1_out, or_2_out;

  Comparator #(.width(16)) comparator_1 (
    .a(A), .b(B), .gt(comparator_1_gt), .eq(comparator_1_eq), .lt(comparator_1_lt));
  or or_1 (or_1_out, comparator_1_gt, comparator_1_eq);
  or or_2 (or_2_out, comparator_1_lt, comparator_1_eq);
  not not_1 (not_1_out, comparator_1_eq);
  Multiplexer #(.select(3)) multiplexer_1 (
    .in0(comparator_1_gt), .in1(comparator_1_eq), .in2(or_1_out), .in3(comparator_1_lt), .in4(or_2_out),
    .in5(not_1_out), .out(RUResult), .sel(RUSel));  // open: in6, in7
endmodule

module REGISTER_16BIT (
  input  [15:0] Data,
  input  WE,
  input  clk,
  input  Reset,
  input  OE,
  output [15:0] Result,
  output [15:0] Dout,
  output [7:0] Eight_LSB,
  output [7:0] Eight_MSB
);

  Register #(.width(16)) register_1 (.D(Data), .en(WE), .clk(clk), .Q(Result), .clr(Reset));
  assign Dout = OE ? Result : 16'bz;  // Controlled_Buffer controlled_buffer_1
  BitSelector #(.group(8), .width(16)) bitselector_1 (.in(Dout), .out(Eight_LSB), .sel(1'b0));
  BitSelector #(.group(8), .width(16)) bitselector_2 (.in(Dout), .out(Eight_MSB), .sel(1'b1));
endmodule

module REGISTER_8BIT (
  input  [7:0] Data,
  input  WE,
  input  clk,
  input  Reset,
  input  OE,
  output [7:0] Result,
  output [7:0] Dout,
  output [3:0] Four_LSBs,
  output [3:0] Four_MSBs
);

  Register register_1 (.D(Data), .en(WE), .clk(clk), .Q(Result), .clr(Reset));
  assign Dout = OE ? Result : 8'bz;  // Controlled_Buffer controlled_buffer_1
  BitSelector #(.group(4)) bitselector_1 (.in(Dout), .out(Four_LSBs), .sel(1'b0));
  BitSelector #(.group(4)) bitselector_2 (.in(Dout), .out(Four_MSBs), .sel(1'b1));
endmodule

module DATAPATH (
  input  [15:0] testing_data,
  input  WE5,
  input  OE4,
  input  OE_testing,
  input  Internal_OE,
  input  WE2,
  input  OE,
  input  WE4,
  input  WE,
  input  OE3,
  input  [3:0] AUSel,
  input  [2:0] RUSel,
  input  OE5,
  input  WE1,
  input  WE3,
  input  OE2,
  output [7:0] out_17,
  output [15:0] IR_content,
  output [15:0] out_19,
  output [15:0] out_20,
  output [15:0] AUResult,
  output out_22,
  output [15:0] out_23,
  output [15:0] out_24
);

  wire clk_out;
  wire [7:0] Instruction_Register_eight_lsb, MAR_dout;
  wire [15:0] ALU_audout;

  Clock clk (.out(clk_out));
  REGISTER_16BIT Instruction_Register (
    .Data(ALU_audout), .WE(WE2), .clk(clk_out), .OE(OE), .Result(IR_content),
    .Eight_LSB(Instruction_Register_eight_lsb));  // open: Reset, Dout, Eight_MSB
  REGISTER_16BIT Register_A (
    .Data(ALU_audout), .WE(WE), .clk(clk_out), .Result(out_20));  // open: Reset, OE, Dout, Eight_LSB, Eight_MSB
  ARITHMETIC_LOGIC_UNIT ALU (
    .OE(OE5), .A(out_20), .B(out_24), .RUSel(RUSel), .AUSel(AUSel), .RUResult(out_22), .AUDout(ALU_audout),
    .AUResult(AUResult));
  REGISTER_16BIT Register_B (
    .Data(ALU_audout), .WE(WE1), .clk(clk_out), .Result(out_24));  // open: Reset, OE, Dout, Eight_LSB, Eight_MSB
  LED D15 (.in(ALU_audout[15]));
  LED D14 (.in(ALU_audout[14]));
  LED D13 (.in(ALU_audout[13]));
  LED D10 (.in(ALU_audout[10]));
  LED D9 (.in(ALU_audout[9]));
  LED D12 (.in(ALU_audout[12]));
  LED D11 (.in(ALU_audout[11]));
  assign ALU_audout = OE_testing ? testing_data : 16'bz;  // Controlled_Buffer controlled_buffer_1
  LED D8 (.in(ALU_audout[8]));
  LED D7 (.in(ALU_audout[7]));
  LED D6 (.in(ALU_audout[6]));
  LED D5 (.in(ALU_audout[5]));
  LED D4 (.in(ALU_audout[4]));
  LED D3 (.in(ALU_audout[3]));
  LED D2 (.in(ALU_audout[2]));
  LED D1 (.in(ALU_audout[1]));
  LED D0 (.in(ALU_audout[0]));
  REGISTER_8BIT MAR (
    .Data(Instruction_Register_eight_lsb), .OE(OE4), .clk(clk_out), .WE(WE5), .Dout(MAR_dout), .Result(out_17));  // open: Reset, Four_LSBs, Four_MSBs
  assign ALU_audout = Internal_OE ? ALU_audout : 16'bz;  // Controlled_Buffer controlled_buffer_2
  REGISTER_16BIT MBR (
    .Data(ALU_audout), .WE(WE4), .clk(clk_out), .OE(OE3), .Result(out_19), .Dout(ALU_audout));  // open: Reset, Eight_LSB, Eight_MSB
  REGISTER_16BIT Output_Register (
    .Data(ALU_audout), .WE(WE3), .clk(clk_out), .OE(OE2), .Result(out_23), .Dout(ALU_audout));  // open: Reset, Eight_LSB, Eight_MSB
  LED led_1 (.in(ALU_audout[15]));
  LED led_2 (.in(ALU_audout[14]));
  LED led_3 (.in(ALU_audout[13]));
  LED led_4 (.in(ALU_audout[12]));
  LED led_5 (.in(ALU_audout[11]));
  LED led_6 (.in(ALU_audout[10]));
  LED led_7 (.in(ALU_audout[9]));
  LED led_8 (.in(ALU_audout[8]));
  LED led_9 (.in(ALU_audout[7]));
  LED led_10 (.in(ALU_audout[6]));
  LED led_11 (.in(ALU_audout[5]));
  LED led_12 (.in(ALU_audout[4]));
  LED led_13 (.in(ALU_audout[3]));
  LED led_14 (.in(ALU_audout[2]));
  LED led_15 (.in(ALU_audout[1]));
  LED led_16 (.in(ALU_audout[0]));

  // Notes on the sheet:
  //   Internal Data Bus
endmodule

module CPU (
  input  [15:0] testing_data,
  input  OE_testing,
  input  [3:0] AUSel,
  input  [2:0] RUSel,
  output [3:0] counter_content,
  output [7:0] out_6,
  output [15:0] IR_content,
  output [15:0] out_8,
  output [15:0] out_9,
  output [15:0] AUResult,
  output out_11,
  output [15:0] out_12,
  output [15:0] out_13,
  output [2:0] sc_content,
  output [31:0] out_15
);

  wire clk_out, control_unit_1_c0, control_unit_1_c1, control_unit_1_c2, control_unit_1_c3,
       control_unit_1_c4, control_unit_1_c5, control_unit_1_c6, control_unit_1_c7, control_unit_1_c8,
       control_unit_1_c9, control_unit_1_c10, control_unit_1_c11, control_unit_1_c12, control_unit_1_c13,
       control_unit_1_c14, control_unit_1_c15;
  wire [2:0] decimal_decoder_1_out_2, decimal_decoder_1_out_6_2, decimal_decoder_2_out_6_2,
       decimal_decoder_3_out_6_2, decimal_decoder_4_out_6_2;
  wire [3:0] controlled_buffer_1_out, decimal_decoder_1_out_2_2, decimal_decoder_1_out_5,
       decimal_decoder_1_out_6, decimal_decoder_2_out_2_2, decimal_decoder_2_out_6, decimal_decoder_3_out_5,
       decimal_decoder_3_out_6, decimal_decoder_4_out_5, decimal_decoder_4_out_6, undriven;
  wire [4:2] decimal_decoder_1_out_5_2, decimal_decoder_2_out_2, decimal_decoder_3_out_5_2,
       decimal_decoder_4_out_5_2;
  wire [6:0] decimal_decoder_1_out_3, decimal_decoder_1_out_4, decimal_decoder_2_out_3,
       decimal_decoder_2_out_4, decimal_decoder_2_out_5, decimal_decoder_3_out_2, decimal_decoder_3_out_3,
       decimal_decoder_3_out_4, decimal_decoder_4_out_2, decimal_decoder_4_out_3, decimal_decoder_4_out_4;
  wire [7:0] bit_extender_1_out, bit_extender_4_out, bitselector_1_out, Instruction_Register_eight_lsb,
       MAR_dout;
  wire [15:0] ARITMETIC_LOGIC_UNIT_audout, ram_1_dout;
  wire [31:0] decimal_decoder_1_1_dout;

  _7_Segment_Display u_7_segment_display_1 (
    .g(decimal_decoder_2_out_5[6]), .f(decimal_decoder_2_out_5[5]), .a(decimal_decoder_2_out_5[0]),
    .b(decimal_decoder_2_out_5[1]), .e(decimal_decoder_2_out_5[4]), .d(decimal_decoder_2_out_5[3]),
    .c(decimal_decoder_2_out_5[2]));  // open: dp
  DECIMAL_DECODER decimal_decoder_1 (
    .Din(AUResult),
    .out_2({decimal_decoder_1_out_2_2[3:2], decimal_decoder_1_out_2, decimal_decoder_1_out_2_2[0], decimal_decoder_1_out_2_2[1]}),
    .out_3(decimal_decoder_1_out_3), .out_4(decimal_decoder_1_out_4),
    .out_5({decimal_decoder_1_out_5[3:2], decimal_decoder_1_out_5_2, decimal_decoder_1_out_5[0], decimal_decoder_1_out_5[1]}),
    .out_6({decimal_decoder_1_out_6[3:2], decimal_decoder_1_out_6_2, decimal_decoder_1_out_6[0], decimal_decoder_1_out_6[1]}));
  _7_Segment_Display u_7_segment_display_2 (
    .g(decimal_decoder_1_out_6[3]), .f(decimal_decoder_1_out_6[2]), .a(decimal_decoder_1_out_6[1]),
    .b(decimal_decoder_1_out_6[0]), .e(decimal_decoder_1_out_6_2[2]), .d(decimal_decoder_1_out_6_2[1]),
    .c(decimal_decoder_1_out_6_2[0]));  // open: dp
  DECIMAL_DECODER decimal_decoder_2 (
    .Din(out_9),
    .out_2({decimal_decoder_2_out_2_2[3:2], decimal_decoder_2_out_2, decimal_decoder_2_out_2_2[0], decimal_decoder_2_out_2_2[1]}),
    .out_3(decimal_decoder_2_out_3), .out_4(decimal_decoder_2_out_4), .out_5(decimal_decoder_2_out_5),
    .out_6({decimal_decoder_2_out_6[3:2], decimal_decoder_2_out_6_2, decimal_decoder_2_out_6[0], decimal_decoder_2_out_6[1]}));
  _7_Segment_Display u_7_segment_display_3 (
    .g(decimal_decoder_2_out_6[3]), .f(decimal_decoder_2_out_6[2]), .a(decimal_decoder_2_out_6[1]),
    .b(decimal_decoder_2_out_6[0]), .e(decimal_decoder_2_out_6_2[2]), .d(decimal_decoder_2_out_6_2[1]),
    .c(decimal_decoder_2_out_6_2[0]));  // open: dp
  _7_Segment_Display u_7_segment_display_4 (
    .g(decimal_decoder_2_out_4[6]), .f(decimal_decoder_2_out_4[5]), .a(decimal_decoder_2_out_4[0]),
    .b(decimal_decoder_2_out_4[1]), .e(decimal_decoder_2_out_4[4]), .d(decimal_decoder_2_out_4[3]),
    .c(decimal_decoder_2_out_4[2]));  // open: dp
  _7_Segment_Display u_7_segment_display_5 (
    .g(decimal_decoder_1_out_5[3]), .f(decimal_decoder_1_out_5[2]), .a(decimal_decoder_1_out_5[1]),
    .b(decimal_decoder_1_out_5[0]), .e(decimal_decoder_1_out_5_2[4]), .d(decimal_decoder_1_out_5_2[3]),
    .c(decimal_decoder_1_out_5_2[2]));  // open: dp
  _7_Segment_Display u_7_segment_display_6 (
    .g(decimal_decoder_1_out_4[6]), .f(decimal_decoder_1_out_4[5]), .a(decimal_decoder_1_out_4[0]),
    .b(decimal_decoder_1_out_4[1]), .e(decimal_decoder_1_out_4[4]), .d(decimal_decoder_1_out_4[3]),
    .c(decimal_decoder_1_out_4[2]));  // open: dp
  _7_Segment_Display u_7_segment_display_7 (
    .g(decimal_decoder_2_out_3[6]), .f(decimal_decoder_2_out_3[5]), .a(decimal_decoder_2_out_3[0]),
    .b(decimal_decoder_2_out_3[1]), .e(decimal_decoder_2_out_3[4]), .d(decimal_decoder_2_out_3[3]),
    .c(decimal_decoder_2_out_3[2]));  // open: dp
  _7_Segment_Display u_7_segment_display_8 (
    .g(decimal_decoder_2_out_2_2[3]), .f(decimal_decoder_2_out_2_2[2]), .a(decimal_decoder_2_out_2_2[1]),
    .b(decimal_decoder_2_out_2_2[0]), .e(decimal_decoder_2_out_2[4]), .d(decimal_decoder_2_out_2[3]),
    .c(decimal_decoder_2_out_2[2]));  // open: dp
  _7_Segment_Display u_7_segment_display_9 (
    .g(decimal_decoder_1_out_3[6]), .f(decimal_decoder_1_out_3[5]), .a(decimal_decoder_1_out_3[0]),
    .b(decimal_decoder_1_out_3[1]), .e(decimal_decoder_1_out_3[4]), .d(decimal_decoder_1_out_3[3]),
    .c(decimal_decoder_1_out_3[2]));  // open: dp
  _7_Segment_Display u_7_segment_display_10 (
    .g(decimal_decoder_1_out_2_2[3]), .f(decimal_decoder_1_out_2_2[2]), .a(decimal_decoder_1_out_2_2[1]),
    .b(decimal_decoder_1_out_2_2[0]), .e(decimal_decoder_1_out_2[2]), .d(decimal_decoder_1_out_2[1]),
    .c(decimal_decoder_1_out_2[0]));  // open: dp
  Clock clk (.out(clk_out));
  DECIMAL_DECODER decimal_decoder_3 (
    .Din(out_13), .out_2(decimal_decoder_3_out_2), .out_3(decimal_decoder_3_out_3),
    .out_4(decimal_decoder_3_out_4),
    .out_5({decimal_decoder_3_out_5[3:2], decimal_decoder_3_out_5_2, decimal_decoder_3_out_5[0], decimal_decoder_3_out_5[1]}),
    .out_6({decimal_decoder_3_out_6[3:2], decimal_decoder_3_out_6_2, decimal_decoder_3_out_6[0], decimal_decoder_3_out_6[1]}));
  Counter #(.max('h3), .width(4)) counter_1 (
    .count(control_unit_1_c1), .clk(clk_out), .D(undriven), .Q(counter_content));  // open: clr, load, up, carry
  _7_Segment_Display u_7_segment_display_11 (
    .g(decimal_decoder_3_out_6[3]), .f(decimal_decoder_3_out_6[2]), .a(decimal_decoder_3_out_6[1]),
    .b(decimal_decoder_3_out_6[0]), .e(decimal_decoder_3_out_6_2[2]), .d(decimal_decoder_3_out_6_2[1]),
    .c(decimal_decoder_3_out_6_2[0]));  // open: dp
  _7_Segment_Display u_7_segment_display_12 (
    .g(decimal_decoder_3_out_5[3]), .f(decimal_decoder_3_out_5[2]), .a(decimal_decoder_3_out_5[1]),
    .b(decimal_decoder_3_out_5[0]), .e(decimal_decoder_3_out_5_2[4]), .d(decimal_decoder_3_out_5_2[3]),
    .c(decimal_decoder_3_out_5_2[2]));  // open: dp
  _7_Segment_Display u_7_segment_display_13 (
    .g(decimal_decoder_3_out_4[6]), .f(decimal_decoder_3_out_4[5]), .a(decimal_decoder_3_out_4[0]),
    .b(decimal_decoder_3_out_4[1]), .e(decimal_decoder_3_out_4[4]), .d(decimal_decoder_3_out_4[3]),
    .c(decimal_decoder_3_out_4[2]));  // open: dp
  DECIMAL_DECODER_1 decimal_decoder_1_1 (.Din(bit_extender_1_out), .Dout(decimal_decoder_1_1_dout));
  _7_Segment_Display u_7_segment_display_14 (
    .g(decimal_decoder_3_out_3[6]), .f(decimal_decoder_3_out_3[5]), .a(decimal_decoder_3_out_3[0]),
    .b(decimal_decoder_3_out_3[1]), .e(decimal_decoder_3_out_3[4]), .d(decimal_decoder_3_out_3[3]),
    .c(decimal_decoder_3_out_3[2]));  // open: dp
  _7_Segment_Display u_7_segment_display_15 (
    .g(decimal_decoder_3_out_2[6]), .f(decimal_decoder_3_out_2[5]), .a(decimal_decoder_3_out_2[0]),
    .b(decimal_decoder_3_out_2[1]), .e(decimal_decoder_3_out_2[4]), .d(decimal_decoder_3_out_2[3]),
    .c(decimal_decoder_3_out_2[2]));  // open: dp
  assign controlled_buffer_1_out = control_unit_1_c0 ? counter_content : 4'bz;  // Controlled_Buffer controlled_buffer_1
  assign bit_extender_1_out = {{4{1'b0}}, counter_content};  // Bit_Extender bit_extender_1
  REGISTER_16BIT Instruction_Register (
    .Data(ARITMETIC_LOGIC_UNIT_audout), .WE(control_unit_1_c7), .clk(clk_out), .OE(control_unit_1_c8),
    .Result(IR_content), .Eight_LSB(Instruction_Register_eight_lsb));  // open: Reset, Dout, Eight_MSB
  REGISTER_16BIT Register_A (
    .Data(ARITMETIC_LOGIC_UNIT_audout), .WE(control_unit_1_c12), .clk(clk_out), .Result(out_9));  // open: Reset, OE, Dout, Eight_LSB, Eight_MSB
  ARITHMETIC_LOGIC_UNIT ARITMETIC_LOGIC_UNIT (
    .OE(control_unit_1_c11), .A(out_9), .B(out_13), .RUSel(RUSel), .AUSel(AUSel), .RUResult(out_11),
    .AUDout(ARITMETIC_LOGIC_UNIT_audout), .AUResult(AUResult));
  REGISTER_16BIT Register_B (
    .Data(ARITMETIC_LOGIC_UNIT_audout), .WE(control_unit_1_c13), .clk(clk_out), .Result(out_13));  // open: Reset, OE, Dout, Eight_LSB, Eight_MSB
  _7_Segment_Display u_7_segment_display_16 (
    .g(decimal_decoder_1_1_dout[3]), .f(decimal_decoder_1_1_dout[2]), .a(decimal_decoder_1_1_dout[1]),
    .b(decimal_decoder_1_1_dout[0]), .e(decimal_decoder_1_1_dout[19]), .d(decimal_decoder_1_1_dout[18]),
    .c(decimal_decoder_1_1_dout[17]), .dp(decimal_decoder_1_1_dout[16]));
  assign Instruction_Register_eight_lsb = {{4{1'b0}}, undriven};  // Bit_Extender bit_extender_2
  assign Instruction_Register_eight_lsb = {{4{1'b0}}, controlled_buffer_1_out};  // Bit_Extender bit_extender_3
  LED D15 (.in(ARITMETIC_LOGIC_UNIT_audout[15]));
  LED D14 (.in(ARITMETIC_LOGIC_UNIT_audout[14]));
  LED D13 (.in(ARITMETIC_LOGIC_UNIT_audout[13]));
  LED D12 (.in(ARITMETIC_LOGIC_UNIT_audout[12]));
  LED D11 (.in(ARITMETIC_LOGIC_UNIT_audout[11]));
  LED D10 (.in(ARITMETIC_LOGIC_UNIT_audout[10]));
  LED D9 (.in(ARITMETIC_LOGIC_UNIT_audout[9]));
  assign ARITMETIC_LOGIC_UNIT_audout = OE_testing ? testing_data : 16'bz;  // Controlled_Buffer controlled_buffer_2
  LED D8 (.in(ARITMETIC_LOGIC_UNIT_audout[8]));
  LED D7 (.in(ARITMETIC_LOGIC_UNIT_audout[7]));
  LED D6 (.in(ARITMETIC_LOGIC_UNIT_audout[6]));
  LED D5 (.in(ARITMETIC_LOGIC_UNIT_audout[5]));
  LED D4 (.in(ARITMETIC_LOGIC_UNIT_audout[4]));
  LED D3 (.in(ARITMETIC_LOGIC_UNIT_audout[3]));
  LED D2 (.in(ARITMETIC_LOGIC_UNIT_audout[2]));
  LED D1 (.in(ARITMETIC_LOGIC_UNIT_audout[1]));
  LED D0 (.in(ARITMETIC_LOGIC_UNIT_audout[0]));
  DECIMAL_DECODER decimal_decoder_4 (
    .Din(out_12), .out_2(decimal_decoder_4_out_2), .out_3(decimal_decoder_4_out_3),
    .out_4(decimal_decoder_4_out_4),
    .out_5({decimal_decoder_4_out_5[3:2], decimal_decoder_4_out_5_2, decimal_decoder_4_out_5[0], decimal_decoder_4_out_5[1]}),
    .out_6({decimal_decoder_4_out_6[3:2], decimal_decoder_4_out_6_2, decimal_decoder_4_out_6[0], decimal_decoder_4_out_6[1]}));
  REGISTER_8BIT MAR (
    .Data(Instruction_Register_eight_lsb), .OE(control_unit_1_c10), .clk(clk_out), .WE(control_unit_1_c9),
    .Dout(MAR_dout), .Result(out_6));  // open: Reset, Four_LSBs, Four_MSBs
  assign ARITMETIC_LOGIC_UNIT_audout = control_unit_1_c5 ? out_8 : 16'bz;  // Controlled_Buffer controlled_buffer_3
  REGISTER_16BIT MBR (
    .Data(ARITMETIC_LOGIC_UNIT_audout), .WE(control_unit_1_c4), .clk(clk_out), .OE(control_unit_1_c6),
    .Result(out_8), .Dout(ARITMETIC_LOGIC_UNIT_audout));  // open: Reset, Eight_LSB, Eight_MSB
  REGISTER_16BIT Output_Register (
    .Data(ARITMETIC_LOGIC_UNIT_audout), .WE(control_unit_1_c15), .clk(clk_out), .OE(control_unit_1_c14),
    .Result(out_12), .Dout(ARITMETIC_LOGIC_UNIT_audout));  // open: Reset, Eight_LSB, Eight_MSB
  _7_Segment_Display u_7_segment_display_17 (
    .g(decimal_decoder_4_out_6[3]), .f(decimal_decoder_4_out_6[2]), .a(decimal_decoder_4_out_6[1]),
    .b(decimal_decoder_4_out_6[0]), .e(decimal_decoder_4_out_6_2[2]), .d(decimal_decoder_4_out_6_2[1]),
    .c(decimal_decoder_4_out_6_2[0]));  // open: dp
  _7_Segment_Display u_7_segment_display_18 (
    .g(decimal_decoder_4_out_5[3]), .f(decimal_decoder_4_out_5[2]), .a(decimal_decoder_4_out_5[1]),
    .b(decimal_decoder_4_out_5[0]), .e(decimal_decoder_4_out_5_2[4]), .d(decimal_decoder_4_out_5_2[3]),
    .c(decimal_decoder_4_out_5_2[2]));  // open: dp
  _7_Segment_Display u_7_segment_display_19 (
    .g(decimal_decoder_4_out_4[6]), .f(decimal_decoder_4_out_4[5]), .a(decimal_decoder_4_out_4[0]),
    .b(decimal_decoder_4_out_4[1]), .e(decimal_decoder_4_out_4[4]), .d(decimal_decoder_4_out_4[3]),
    .c(decimal_decoder_4_out_4[2]));  // open: dp
  _7_Segment_Display u_7_segment_display_20 (
    .g(decimal_decoder_4_out_3[6]), .f(decimal_decoder_4_out_3[5]), .a(decimal_decoder_4_out_3[0]),
    .b(decimal_decoder_4_out_3[1]), .e(decimal_decoder_4_out_3[4]), .d(decimal_decoder_4_out_3[3]),
    .c(decimal_decoder_4_out_3[2]));  // open: dp
  _7_Segment_Display u_7_segment_display_21 (
    .g(decimal_decoder_4_out_2[6]), .f(decimal_decoder_4_out_2[5]), .a(decimal_decoder_4_out_2[0]),
    .b(decimal_decoder_4_out_2[1]), .e(decimal_decoder_4_out_2[4]), .d(decimal_decoder_4_out_2[3]),
    .c(decimal_decoder_4_out_2[2]));  // open: dp
  LED led_1 (.in(ARITMETIC_LOGIC_UNIT_audout[15]));
  LED led_2 (.in(ARITMETIC_LOGIC_UNIT_audout[14]));
  LED led_3 (.in(ARITMETIC_LOGIC_UNIT_audout[13]));
  LED led_4 (.in(ARITMETIC_LOGIC_UNIT_audout[12]));
  LED led_5 (.in(ARITMETIC_LOGIC_UNIT_audout[11]));
  LED led_6 (.in(ARITMETIC_LOGIC_UNIT_audout[10]));
  LED led_7 (.in(ARITMETIC_LOGIC_UNIT_audout[9]));
  LED led_8 (.in(ARITMETIC_LOGIC_UNIT_audout[8]));
  LED led_9 (.in(ARITMETIC_LOGIC_UNIT_audout[7]));
  LED led_10 (.in(ARITMETIC_LOGIC_UNIT_audout[6]));
  LED led_11 (.in(ARITMETIC_LOGIC_UNIT_audout[5]));
  LED led_12 (.in(ARITMETIC_LOGIC_UNIT_audout[4]));
  LED led_13 (.in(ARITMETIC_LOGIC_UNIT_audout[3]));
  LED led_14 (.in(ARITMETIC_LOGIC_UNIT_audout[2]));
  LED led_15 (.in(ARITMETIC_LOGIC_UNIT_audout[1]));
  LED led_16 (.in(ARITMETIC_LOGIC_UNIT_audout[0]));
  RAM #(.dataWidth(16), .enables("line")) ram_1 (
    .addr(MAR_dout), .we(control_unit_1_c2), .clk(clk_out), .din(ARITMETIC_LOGIC_UNIT_audout),
    .dout(ram_1_dout));
  Counter #(.max('h5), .width(3)) Step_Counter (.clk(clk_out), .Q(sc_content));  // open: clr, load, up, count, D, carry
  assign ARITMETIC_LOGIC_UNIT_audout = control_unit_1_c3 ? ram_1_dout : 16'bz;  // Controlled_Buffer controlled_buffer_4
  BitSelector #(.group(8), .width(16)) bitselector_1 (.in(IR_content), .out(bitselector_1_out), .sel(1'b1));
  assign bit_extender_4_out = {{5{1'b0}}, sc_content};  // Bit_Extender bit_extender_4
  DECIMAL_DECODER_1 decimal_decoder_1_2 (.Din(bit_extender_4_out), .Dout(out_15));
  _7_Segment_Display u_7_segment_display_22 (
    .g(out_15[3]), .f(out_15[2]), .a(out_15[1]), .b(out_15[0]), .e(out_15[19]), .d(out_15[18]),
    .c(out_15[17]), .dp(out_15[16]));
  CONTROL_UNIT control_unit_1 (
    .OPC5(bitselector_1_out[5]), .OPC4(bitselector_1_out[4]), .OPC3(bitselector_1_out[3]),
    .OPC2(bitselector_1_out[2]), .OPC1(bitselector_1_out[1]), .OPC0(bitselector_1_out[0]),
    .SC2(sc_content[2]), .SC1(sc_content[1]), .SC0(sc_content[0]), .OPC7(bitselector_1_out[7]),
    .OPC6(bitselector_1_out[6]), .C2(control_unit_1_c2), .C3(control_unit_1_c3), .C4(control_unit_1_c4),
    .C5(control_unit_1_c5), .C6(control_unit_1_c6), .C7(control_unit_1_c7), .C8(control_unit_1_c8),
    .C9(control_unit_1_c9), .C10(control_unit_1_c10), .C11(control_unit_1_c11), .C12(control_unit_1_c12),
    .C13(control_unit_1_c13), .C14(control_unit_1_c14), .C15(control_unit_1_c15), .C0(control_unit_1_c0),
    .C1(control_unit_1_c1));

  // Notes on the sheet:
  //   Internal Data Bus
  //   Internal data bus
  //   GODFRED SAFO OFORI -  22046644
  //   CHRISTOPHER Y.E. MAWULI -  22071976
  //   GROUP 25
  //   External Data Bus
endmodule

module DECIMAL_DECODER (
  input  [15:0] Din,
  output [6:0] out_2,
  output [6:0] out_3,
  output [6:0] out_4,
  output [6:0] out_5,
  output [6:0] out_6
);

  ROM #(.addrWidth(16), .dataWidth(35)) rom_1 (.addr(Din), .data({out_6, out_5, out_4, out_3, out_2}));

  // Notes on the sheet:
  //   contents of rom_1 (hex, n*v repeats v):
  //   3f7efdfbf 3f7efdf86 3f7efdfdb 3f7efdfcf 3f7efdfe6 3f7efdfed 3f7efdffd 3f7efdf87 3f7efdfff 3f7efdfef
  //   3f7efc33f 3f7efc306 3f7efc35b 3f7efc34f 3f7efc366 3f7efc36d 3f7efc37d 3f7efc307 3f7efc37f 3f7efc36f
  //   3f7efedbf 3f7efed86 3f7efeddb 3f7efedcf 3f7efede6 3f7efeded 3f7efedfd 3f7efed87 3f7efedff 3f7efedef
  //   3f7efe7bf 3f7efe786 3f7efe7db 3f7efe7cf 3f7efe7e6 3f7efe7ed 3f7efe7fd 3f7efe787 3f7efe7ff 3f7efe7ef
  //   3f7eff33f 3f7eff306 3f7eff35b 3f7eff34f 3f7eff366 3f7eff36d 3f7eff37d 3f7eff307 3f7eff37f 3f7eff36f
  //   3f7eff6bf 3f7eff686 3f7eff6db 3f7eff6cf 3f7eff6e6 3f7eff6ed 3f7eff6fd 3f7eff687 3f7eff6ff 3f7eff6ef
  //   3f7effebf 3f7effe86 3f7effedb 3f7effecf 3f7effee6 3f7effeed 3f7effefd 3f7effe87 3f7effeff 3f7effeef
  //   3f7efc3bf 3f7efc386 3f7efc3db 3f7efc3cf 3f7efc3e6 3f7efc3ed 3f7efc3fd 3f7efc387 3f7efc3ff 3f7efc3ef
  //   3f7efffbf 3f7efff86 3f7efffdb 3f7efffcf 3f7efffe6 3f7efffed 3f7effffd 3f7efff87 3f7efffff 3f7efffef
  //   3f7eff7bf 3f7eff786 3f7eff7db 3f7eff7cf 3f7eff7e6 3f7eff7ed 3f7eff7fd 3f7eff787 3f7eff7ff 3f7eff7ef
  //   3f7e19fbf 3f7e19f86 3f7e19fdb 3f7e19fcf 3f7e19fe6 3f7e19fed 3f7e19ffd 3f7e19f87 3f7e19fff 3f7e19fef
  //   3f7e1833f 3f7e18306 3f7e1835b 3f7e1834f 3f7e18366 3f7e1836d 3f7e1837d 3f7e18307 3f7e1837f 3f7e1836f
  //   3f7e1adbf 3f7e1ad86 3f7e1addb 3f7e1adcf 3f7e1ade6 3f7e1aded 3f7e1adfd 3f7e1ad87 3f7e1adff 3f7e1adef
  //   3f7e1a7bf 3f7e1a786 3f7e1a7db 3f7e1a7cf 3f7e1a7e6 3f7e1a7ed 3f7e1a7fd 3f7e1a787 3f7e1a7ff 3f7e1a7ef
  //   3f7e1b33f 3f7e1b306 3f7e1b35b 3f7e1b34f 3f7e1b366 3f7e1b36d 3f7e1b37d 3f7e1b307 3f7e1b37f 3f7e1b36f
  //   3f7e1b6bf 3f7e1b686 3f7e1b6db 3f7e1b6cf 3f7e1b6e6 3f7e1b6ed 3f7e1b6fd 3f7e1b687 3f7e1b6ff 3f7e1b6ef
  //   3f7e1bebf 3f7e1be86 3f7e1bedb 3f7e1becf 3f7e1bee6 3f7e1beed 3f7e1befd 3f7e1be87 3f7e1beff 3f7e1beef
  //   3f7e183bf 3f7e18386 3f7e183db 3f7e183cf 3f7e183e6 3f7e183ed 3f7e183fd 3f7e18387 3f7e183ff 3f7e183ef
  //   3f7e1bfbf 3f7e1bf86 3f7e1bfdb 3f7e1bfcf 3f7e1bfe6 3f7e1bfed 3f7e1bffd 3f7e1bf87 3f7e1bfff 3f7e1bfef
  //   3f7e1b7bf 3f7e1b786 3f7e1b7db 3f7e1b7cf 3f7e1b7e6 3f7e1b7ed 3f7e1b7fd 3f7e1b787 3f7e1b7ff 3f7e1b7ef
  //   3f7f6dfbf 3f7f6df86 3f7f6dfdb 3f7f6dfcf 3f7f6dfe6 3f7f6dfed 3f7f6dffd 3f7f6df87 3f7f6dfff 3f7f6dfef
  //   3f7f6c33f 3f7f6c306 3f7f6c35b 3f7f6c34f 3f7f6c366 3f7f6c36d 3f7f6c37d 3f7f6c307 3f7f6c37f 3f7f6c36f
  //   3f7f6edbf 3f7f6ed86 3f7f6eddb 3f7f6edcf 3f7f6ede6 3f7f6eded 3f7f6edfd 3f7f6ed87 3f7f6edff 3f7f6edef
  //   3f7f6e7bf 3f7f6e786 3f7f6e7db 3f7f6e7cf 3f7f6e7e6 3f7f6e7ed 3f7f6e7fd 3f7f6e787 3f7f6e7ff 3f7f6e7ef
  //   3f7f6f33f 3f7f6f306 3f7f6f35b 3f7f6f34f 3f7f6f366 3f7f6f36d 3f7f6f37d 3f7f6f307 3f7f6f37f 3f7f6f36f
  //   3f7f6f6bf 3f7f6f686 3f7f6f6db 3f7f6f6cf 3f7f6f6e6 3f7f6f6ed 3f7f6f6fd 3f7f6f687 3f7f6f6ff 3f7f6f6ef
  //   3f7f6febf 3f7f6fe86 3f7f6fedb 3f7f6fecf 3f7f6fee6 3f7f6feed 3f7f6fefd 3f7f6fe87 3f7f6feff 3f7f6feef
  //   3f7f6c3bf 3f7f6c386 3f7f6c3db 3f7f6c3cf 3f7f6c3e6 3f7f6c3ed 3f7f6c3fd 3f7f6c387 3f7f6c3ff 3f7f6c3ef
  //   3f7f6ffbf 3f7f6ff86 3f7f6ffdb 3f7f6ffcf 3f7f6ffe6 3f7f6ffed 3f7f6fffd 3f7f6ff87 3f7f6ffff 3f7f6ffef
  //   3f7f6f7bf 3f7f6f786 3f7f6f7db 3f7f6f7cf 3f7f6f7e6 3f7f6f7ed 3f7f6f7fd 3f7f6f787 3f7f6f7ff 3f7f6f7ef
  //   3f7f3dfbf 3f7f3df86 3f7f3dfdb 3f7f3dfcf 3f7f3dfe6 3f7f3dfed 3f7f3dffd 3f7f3df87 3f7f3dfff 3f7f3dfef
  //   3f7f3c33f 3f7f3c306 3f7f3c35b 3f7f3c34f 3f7f3c366 3f7f3c36d 3f7f3c37d 3f7f3c307 3f7f3c37f 3f7f3c36f
  //   3f7f3edbf 3f7f3ed86 3f7f3eddb 3f7f3edcf 3f7f3ede6 3f7f3eded 3f7f3edfd 3f7f3ed87 3f7f3edff 3f7f3edef
  //   3f7f3e7bf 3f7f3e786 3f7f3e7db 3f7f3e7cf 3f7f3e7e6 3f7f3e7ed 3f7f3e7fd 3f7f3e787 3f7f3e7ff 3f7f3e7ef
  //   3f7f3f33f 3f7f3f306 3f7f3f35b 3f7f3f34f 3f7f3f366 3f7f3f36d 3f7f3f37d 3f7f3f307 3f7f3f37f 3f7f3f36f
  //   3f7f3f6bf 3f7f3f686 3f7f3f6db 3f7f3f6cf 3f7f3f6e6 3f7f3f6ed 3f7f3f6fd 3f7f3f687 3f7f3f6ff 3f7f3f6ef
  //   3f7f3febf 3f7f3fe86 3f7f3fedb 3f7f3fecf 3f7f3fee6 3f7f3feed 3f7f3fefd 3f7f3fe87 3f7f3feff 3f7f3feef
  //   3f7f3c3bf 3f7f3c386 3f7f3c3db 3f7f3c3cf 3f7f3c3e6 3f7f3c3ed 3f7f3c3fd 3f7f3c387 3f7f3c3ff 3f7f3c3ef
  //   3f7f3ffbf 3f7f3ff86 3f7f3ffdb 3f7f3ffcf 3f7f3ffe6 3f7f3ffed 3f7f3fffd 3f7f3ff87 3f7f3ffff 3f7f3ffef
  //   3f7f3f7bf 3f7f3f786 3f7f3f7db 3f7f3f7cf 3f7f3f7e6 3f7f3f7ed 3f7f3f7fd 3f7f3f787 3f7f3f7ff 3f7f3f7ef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
endmodule

module DECIMAL_DECODER_1 (
  input  [7:0] Din,
  output [31:0] Dout
);

  ROM #(.dataWidth(32)) rom_1 (
    .addr(Din),
    .data({Dout[31:28], Dout[15:12], Dout[27:24], Dout[11:8], Dout[23:20], Dout[7:4], Dout[19:16], Dout[3:0]}));

  // Notes on the sheet:
  //   contents of rom_1 (hex, n*v repeats v):
  //   e7 21 cb 6b 2d 6e ee 23 ef 2f 21e7 2121 21cb 216b 212d 216e 21ee 2123 21ef 212f cbe7 cb21 cbcb cb6b
  //   cb2d cb6e cbee cb23 cbef cb2f 6be7 6b21 6bcb 6b6b 6b2d 6b6e 6bee 6b23 6bef 6b2f 2de7 2d21 2dcb 2d6b
  //   2d2d 2d6e 2dee 2d23 2def 2d2f 6ee7 6e21 6ecb 6e6b 6e2d 6e6e 6eee 6e23 6eef 6e2f eee7 ee21 eecb ee6b
  //   ee2d ee6e eeee ee23 eeef ee2f 23e7 2321 23cb 236b 232d 236e 23ee 2323 23ef 232f efe7 ef21 efcb ef6b
  //   ef2d ef6e efee ef23 efef ef2f 2fe7 2f21 2fcb 2f6b 2f2d 2f6e 2fee 2f23 2fef 2f2f 21e7e7 21e721 21e7cb
  //   21e76b 21e72d 21e76e 21e7ee 21e723 21e7ef 21e72f 2121e7 212121 2121cb 21216b 21212d 21216e 2121ee
  //   212123 2121ef 21212f 21cbe7 21cb21 21cbcb 21cb6b 21cb2d 21cb6e 21cbee 21cb23 21cbef 21cb2f 216be7
  //   216b21 216bcb 216b6b 216b2d 216b6e 216bee 216b23 216bef 216b2f 212de7 212d21 212dcb 212d6b 212d2d
  //   212d6e 212dee 212d23 212def 212d2f 216ee7 216e21 216ecb 216e6b 216e2d 216e6e 216eee 216e23 216eef
  //   216e2f 21eee7 21ee21 21eecb 21ee6b 21ee2d 21ee6e 21eeee 21ee23 21eeef 21ee2f 2123e7 212321 2123cb
  //   21236b 21232d 21236e 2123ee 212323 2123ef 21232f 21efe7 21ef21 21efcb 21ef6b 21ef2d 21ef6e 21efee
  //   21ef23 21efef 21ef2f 212fe7 212f21 212fcb 212f6b 212f2d 212f6e 212fee 212f23 212fef 212f2f cbe7e7
  //   cbe721 cbe7cb cbe76b cbe72d cbe76e cbe7ee cbe723 cbe7ef cbe72f cb21e7 cb2121 cb21cb cb216b cb212d
  //   cb216e cb21ee cb2123 cb21ef cb212f cbcbe7 cbcb21 cbcbcb cbcb6b cbcb2d cbcb6e cbcbee cbcb23 cbcbef
  //   cbcb2f cb6be7 cb6b21 cb6bcb cb6b6b cb6b2d cb6b6e cb6bee cb6b23 cb6bef cb6b2f cb2de7 cb2d21 cb2dcb
  //   cb2d6b cb2d2d cb2d6e cb2dee cb2d23 cb2def cb2d2f cb6ee7 cb6e21 cb6ecb cb6e6b cb6e2d cb6e6e
endmodule

module CONTROL_UNIT (
  input  OPC7,
  input  OPC6,
  input  OPC5,
  input  OPC4,
  input  OPC3,
  input  OPC2,
  input  OPC1,
  input  OPC0,
  input  SC2,
  input  SC1,
  input  SC0,
  output C0,
  output C1,
  output C2,
  output C3,
  output C4,
  output C5,
  output C6,
  output C7,
  output C8,
  output C9,
  output C10,
  output C11,
  output C12,
  output C13,
  output C14,
  output C15
);

  wire and_4_out, and_5_out, and_6_out, and_7_out, and_8_out, and_9_out, and_10_out, and_13_out, and_14_out,
       and_15_out, and_16_out, and_17_out, and_18_out, and_19_out, and_20_out, not_1_out, not_2_out,
       not_3_out, not_4_out, not_5_out;

  not not_1 (not_1_out, OPC1);
  not not_2 (not_2_out, OPC0);
  not not_3 (not_3_out, SC2);
  not not_4 (not_4_out, SC1);
  not not_5 (not_5_out, SC0);
  and and_1 (C0, not_3_out, not_4_out, not_5_out);
  and and_2 (C1, not_3_out, not_4_out, SC0);
  and and_3 (C2, OPC1, OPC0, SC2);
  and and_4 (and_4_out, not_3_out, not_4_out, SC0);
  and and_5 (and_5_out, not_1_out, SC2, not_4_out, not_5_out);
  and and_6 (and_6_out, not_3_out, not_4_out, SC0);
  and and_7 (and_7_out, not_1_out, SC2, not_4_out, not_5_out);
  and and_8 (and_8_out, OPC1, OPC0, SC0);
  and and_9 (and_9_out, not_3_out, SC1, not_5_out);
  and and_10 (and_10_out, not_1_out, SC2, not_4_out, SC0);
  and and_11 (C6, OPC1, OPC0, SC2);
  and and_12 (C7, not_3_out, SC1, not_5_out);
  and and_13 (and_13_out, not_1_out, not_3_out, SC1, SC0);
  and and_14 (and_14_out, OPC0, not_3_out, SC1, SC0);
  and and_15 (and_15_out, not_3_out, not_4_out, not_5_out);
  and and_16 (and_16_out, not_1_out, not_3_out, SC1, SC0);
  and and_17 (and_17_out, OPC0, not_3_out, SC1, SC0);
  and and_18 (and_18_out, not_3_out, not_4_out, SC0);
  and and_19 (and_19_out, not_1_out, SC2, not_4_out, not_5_out);
  and and_20 (and_20_out, OPC1, OPC0, SC2);
  and and_21 (C11, OPC1, not_2_out, not_3_out, SC1, SC0);
  and and_22 (C12, not_1_out, not_2_out, SC2, not_4_out, SC0);
  and and_23 (C13, OPC0, SC2, not_4_out, SC0);
  and and_24 (C14, OPC1, OPC0, SC1, SC0);
  and and_25 (C15, OPC1, not_2_out, not_3_out, SC1, SC0);
  or or_1 (C3, and_4_out, and_5_out);
  or or_2 (C4, and_6_out, and_7_out, and_8_out);
  or or_3 (C5, and_9_out, and_10_out);
  or or_4 (C8, and_13_out, and_14_out);
  or or_5 (C9, and_15_out, and_16_out, and_17_out);
  or or_6 (C10, and_18_out, and_19_out, and_20_out);
endmodule
